// Logisim project Project2Given.circ as structural Verilog: 4 circuits, main circuit main
module main (
);

  wire and_1_out, and_2_out, B0, B1, B2, B3, B4, B5, B6, B7, B8, B9, BL, BU, C0, C1, C2, CLK, L1_l, L1_u,
       not_1_out, or_8_out, P1_v, R0, R1, R3, R4, Valid;
  wire [2:0] counter_1_q;
  wire [3:0] IB1_c0, P1_b0, register_2_q, register_3_q, register_4_q, register_5_q;

  Button n1 (.out(B1));
  Button n4 (.out(B4));
  Button n7 (.out(B7));
  Button L (.out(BL));
  Button n3 (.out(B3));
  Button n2 (.out(B2));
  Button n6 (.out(B6));
  Button n5 (.out(B5));
  Button n9 (.out(B9));
  Button n8 (.out(B8));
  Button U (.out(BU));
  Button n0 (.out(B0));
  or or_1 (R0, B3, B2, B1);
  or or_2 (R1, B6, B5, B4);
  or or_3 (R3, B9, B8, B7);
  or or_4 (R4, BU, B0, BL);
  or or_5 (C0, B1, B4, B7, BL);
  or or_6 (C1, B2, B5, B8, B0);
  or or_7 (C2, B3, B6, B9, BU);
  Clock clock_1 (.out(CLK));
  nand nand_1 (Valid, IB1_c0[0], IB1_c0[1], IB1_c0[2], IB1_c0[3]);
  // Probe on P1_b0
  Panel P1 (
    .R0(R0), .R1(R1), .R2(R3), .R3(R4), .C0(C0), .C1(C1), .C2(C2), .B0(P1_b0[0]), .B1(P1_b0[1]),
    .B2(P1_b0[2]), .B3(P1_b0[3]), .V(P1_v));
  LED Press (.in(P1_v));
  // Probe on IB1_c0
  InputBuffer IB1 (
    .B0(P1_b0[0]), .B1(P1_b0[1]), .B2(P1_b0[2]), .B3(P1_b0[3]), .V(P1_v), .CLK(not_1_out), .C0(IB1_c0[0]),
    .C1(IB1_c0[1]), .C2(IB1_c0[2]), .C3(IB1_c0[3]));
  not not_1 (not_1_out, CLK);
  Register #(.width(4)) register_1 (.D(register_2_q), .en(Valid), .clk(CLK));  // open: Q, clr
  Lock L1 (.C0(IB1_c0[0]), .C1(IB1_c0[1]), .C2(IB1_c0[2]), .C3(IB1_c0[3]), .CLK(CLK), .U(L1_u), .L(L1_l));
  Counter #(.max('h7), .width(3)) counter_1 (
    .count(or_8_out), .Q(counter_1_q), .up(L1_l), .clk(CLK));  // open: load, D, carry, clr
  or or_8 (or_8_out, L1_u, L1_l);
  Register #(.width(4)) register_2 (.D(register_3_q), .en(Valid), .clk(CLK), .Q(register_2_q));  // open: clr
  LED Unlocked (.in(and_1_out));
  and and_1 (and_1_out, ~counter_1_q[0], ~counter_1_q[1], ~counter_1_q[2]);  // AND_Gate
  Register #(.width(4)) register_3 (.D(register_4_q), .en(Valid), .clk(CLK), .Q(register_3_q));  // open: clr
  LED Locked (.in(and_2_out));
  and and_2 (and_2_out, ~counter_1_q[0], ~counter_1_q[1], counter_1_q[2]);  // AND_Gate
  Register #(.width(4)) register_4 (.D(register_5_q), .en(Valid), .clk(CLK), .Q(register_4_q));  // open: clr
  Register #(.width(4)) register_5 (.D(IB1_c0), .en(Valid), .clk(CLK), .Q(register_5_q));  // open: clr
endmodule

module Panel (
  input  R0,
  input  R1,
  input  R2,
  input  R3,
  input  C0,
  input  C1,
  input  C2,
  output B0,
  output B1,
  output B2,
  output B3,
  output V
);

  wire L_out, n0_out, n1_out, n2_out, n3_out, n4_out, n5_out, n6_out, n7_out, n8_out, n9_out, U_out;

  and n1 (n1_out, R0, C0);
  and n2 (n2_out, R0, C1);
  and n3 (n3_out, R0, C2);
  and n4 (n4_out, R1, C0);
  and n5 (n5_out, R1, C1);
  and n6 (n6_out, R1, C2);
  and n7 (n7_out, R2, C0);
  and n8 (n8_out, R2, C1);
  and n9 (n9_out, R2, C2);
  and L (L_out, R3, C0);
  and n0 (n0_out, R3, C1);
  and U (U_out, R3, C2);
  ExactlyOne xor_1 (.out(B0), .in0(n1_out), .in1(n3_out), .in2(n5_out), .in3(n7_out), .in4(n9_out), .in5(U_out));
  ExactlyOne xor_2 (
    .out(B1), .in0(n2_out), .in1(n3_out), .in2(n5_out), .in3(U_out), .in4(n6_out), .in5(n7_out), .in6(L_out));
  ExactlyOne xor_3 (.out(B2), .in0(n4_out), .in1(n5_out), .in2(n6_out), .in3(n7_out));
  ExactlyOne xor_4 (.out(B3), .in0(n8_out), .in1(n9_out), .in2(L_out), .in3(U_out));
  ExactlyOne xor_5 (
    .out(V), .in0(n1_out), .in1(n2_out), .in2(n3_out), .in3(n4_out), .in4(n5_out), .in5(n6_out),
    .in6(n7_out), .in7(n8_out), .in8(n9_out), .in9(L_out), .in10(n0_out), .in11(U_out));
endmodule

module InputBuffer (
  input  B0,
  input  B1,
  input  B2,
  input  B3,
  input  V,
  input  CLK,
  output C0,
  output C1,
  output C2,
  output C3
);

  wire and_1_out, and_2_out, and_3_out, d_ff_1_q, d_ff_1_qn, d_ff_2_qn, NO_S, or_1_out;

  Multiplexer multiplexer_1 (.in0(1'b1), .in1(B0), .out(C0), .sel(NO_S));
  Multiplexer multiplexer_2 (.in0(1'b1), .in1(B1), .out(C1), .sel(NO_S));
  Multiplexer multiplexer_3 (.in0(1'b1), .in1(B2), .out(C2), .sel(NO_S));
  Multiplexer multiplexer_4 (.in0(1'b1), .in1(B3), .out(C3), .sel(NO_S));
  and and_1 (and_1_out, d_ff_1_q, V);
  and and_2 (and_2_out, NO_S, V);
  or or_1 (or_1_out, and_1_out, and_2_out);
  and and_3 (and_3_out, d_ff_1_qn, V, d_ff_2_qn);
  D_Flip_Flop d_ff_1 (.D(or_1_out), .clk(CLK), .Q(d_ff_1_q), .Qn(d_ff_1_qn));  // open: preset, reset
  D_Flip_Flop d_ff_2 (.D(and_3_out), .clk(CLK), .Q(NO_S), .Qn(d_ff_2_qn));  // open: preset, reset
endmodule

module Lock (
  input  C0,
  input  C1,
  input  C2,
  input  C3,
  input  CLK,
  output U,
  output L
);

  wire and_3_out, and_7_out, and_8_out, and_10_out, and_11_out, and_13_out, and_14_out, and_15_out,
       and_16_out, and_17_out, and_18_out, and_19_out, and_20_out, and_21_out, and_22_out, and_25_out,
       and_27_out, and_28_out, and_29_out, and_30_out, and_31_out, and_32_out, and_33_out, and_34_out,
       and_35_out, and_36_out, and_37_out, Changemain, Comparing, d_ff_1_q, d_ff_5_q, Digit, EN_A, EN_B,
       EN_C, EN_D, EN_W, EN_X, EN_Y, EN_Z, Lock, LOCKING, Nocode, not_1_out, not_2_out, not_3_out, not_4_out,
       not_5_out, not_6_out, not_7_out, not_8_out, ST_A, ST_B, ST_C, ST_D, ST_W, ST_X, ST_Y, ST_Z, TOLOCKED,
       TOLOCKING, TOUNLOCKED, TOUNLOCKING, Unlock, UNLOCKING;
  wire [1:0] counter_1_q, counter_2_q, counter_3_q;
  wire [3:0] and_12_out, register_1_q, register_2_q, register_3_q, register_4_q, register_5_q, xnor_1_out,
       xnor_2_out, xnor_3_out;

  not not_1 (not_1_out, C2);
  not not_2 (not_2_out, C0);
  not not_3 (not_3_out, C3);
  not not_4 (not_4_out, C1);
  and and_1 (Lock, C3, not_1_out, C1, not_2_out);
  and and_2 (Unlock, C3, not_1_out, C1, C0);
  and and_3 (and_3_out, not_1_out, not_4_out);
  and and_4 (Nocode, C3, C2, C1, C0);
  Counter #(.max('h3), .width(2)) counter_1 (
    .count(Changemain), .Q(counter_1_q), .clk(CLK));  // open: load, D, carry, up, clr
  Counter #(.max('h3), .width(2)) counter_2 (
    .count(LOCKING), .Q(counter_2_q), .clk(CLK));  // open: load, D, carry, up, clr
  Counter #(.max('h3), .width(2)) counter_3 (
    .count(UNLOCKING), .Q(counter_3_q), .clk(CLK));  // open: load, D, carry, up, clr
  or or_1 (Digit, not_3_out, and_3_out);
  Decoder #(.select(2)) decoder_1 (.out0(U), .out1(LOCKING), .out2(L), .out3(UNLOCKING), .sel(counter_1_q), .en(1'b1));
  and and_5 (TOLOCKED, counter_2_q[0], counter_2_q[1]);
  and and_6 (TOUNLOCKED, counter_3_q[0], counter_3_q[1]);
  or or_2 (Changemain, TOLOCKING, TOLOCKED, TOUNLOCKING, TOUNLOCKED);
  not not_5 (not_5_out, EN_A);
  not not_6 (not_6_out, L);
  and and_7 (and_7_out, Digit, U);
  D_Flip_Flop d_ff_1 (.D(not_5_out), .clk(CLK), .Q(d_ff_1_q), .Qn(ST_A), .reset(not_6_out));  // open: preset
  D_Flip_Flop d_ff_2 (.D(EN_B), .clk(CLK), .Q(ST_B), .reset(not_6_out));  // open: Qn, preset
  D_Flip_Flop d_ff_3 (.D(EN_C), .clk(CLK), .Q(ST_C), .reset(not_6_out));  // open: Qn, preset
  D_Flip_Flop d_ff_4 (.D(EN_D), .clk(CLK), .Q(ST_D), .reset(not_6_out));  // open: Qn, preset
  Register #(.width(4)) register_1 (.D({C3, C2, C1, C0}), .en(Digit), .clk(CLK), .Q(register_1_q));  // open: clr
  Register #(.width(4)) register_2 (.D({C3, C2, C1, C0}), .en(and_7_out), .clk(CLK), .Q(register_2_q));  // open: clr
  assign xnor_1_out = ~({C3, C2, C1, C0} ^ register_2_q);  // XNOR_Gate xnor_1, 4 bits wide
  and and_8 (and_8_out, Digit, U);
  Register #(.width(4)) register_3 (.D(register_1_q), .en(Digit), .clk(CLK), .Q(register_3_q));  // open: clr
  Register #(.width(4)) register_4 (.D(register_1_q), .en(and_8_out), .clk(CLK), .Q(register_4_q));  // open: clr
  not not_7 (not_7_out, EN_W);
  not not_8 (not_8_out, U);
  and and_9 (Comparing, ST_D, Digit);
  assign xnor_2_out = ~(register_1_q ^ register_4_q);  // XNOR_Gate xnor_2, 4 bits wide
  Register #(.width(4)) register_5 (.D(register_3_q), .en(and_8_out), .clk(CLK), .Q(register_5_q));  // open: clr
  D_Flip_Flop d_ff_5 (.D(not_7_out), .clk(CLK), .Q(d_ff_5_q), .Qn(ST_W), .reset(not_8_out));  // open: preset
  D_Flip_Flop d_ff_6 (.D(EN_X), .clk(CLK), .Q(ST_X), .reset(not_8_out));  // open: Qn, preset
  D_Flip_Flop d_ff_7 (.D(EN_Y), .clk(CLK), .Q(ST_Y), .reset(not_8_out));  // open: Qn, preset
  D_Flip_Flop d_ff_8 (.D(EN_Z), .clk(CLK), .Q(ST_Z), .reset(not_8_out));  // open: Qn, preset
  and and_10 (and_10_out, ST_X, Lock);
  and and_11 (and_11_out, ST_Z, Digit);
  or or_3 (TOLOCKING, and_10_out, and_11_out);
  assign xnor_3_out = ~(register_3_q ^ register_5_q);  // XNOR_Gate xnor_3, 4 bits wide
  assign and_12_out = xnor_3_out & xnor_2_out & xnor_1_out;  // AND_Gate and_12, 4 bits wide
  and and_13 (and_13_out, ST_W, Unlock);
  and and_14 (and_14_out, ST_W, Digit);
  and and_15 (and_15_out, ST_W, Nocode);
  and and_16 (and_16_out, ST_Y, Unlock);
  and and_17 (and_17_out, ST_Z, Unlock);
  and and_18 (and_18_out, ST_X, Unlock);
  and and_19 (and_19_out, ST_W, Lock);
  and and_20 (and_20_out, ST_X, Nocode);
  and and_21 (and_21_out, ST_Y, Lock);
  and and_22 (and_22_out, ST_Z, Lock);
  and and_23 (EN_Y, ST_X, Digit);
  and and_24 (EN_Z, ST_Y, Digit);
  or or_4 (EN_X, and_19_out, and_20_out, and_21_out, and_22_out);
  and and_25 (and_25_out, and_12_out[0], and_12_out[1], and_12_out[2], and_12_out[3]);
  or or_5 (EN_W, and_13_out, and_14_out, and_15_out, and_16_out, and_17_out, and_18_out);
  and and_26 (TOUNLOCKING, and_25_out, L, Comparing);
  and and_27 (and_27_out, ST_A, Lock);
  and and_28 (and_28_out, ST_A, Digit);
  and and_29 (and_29_out, ST_A, Nocode);
  and and_30 (and_30_out, ST_B, Lock);
  and and_31 (and_31_out, ST_C, Lock);
  and and_32 (and_32_out, ST_D, Lock);
  and and_33 (and_33_out, ST_A, Unlock);
  and and_34 (and_34_out, ST_B, Nocode);
  and and_35 (and_35_out, ST_B, Unlock);
  and and_36 (and_36_out, ST_C, Unlock);
  and and_37 (and_37_out, ST_D, Unlock);
  and and_38 (EN_C, ST_B, Digit);
  and and_39 (EN_D, ST_C, Digit);
  or or_6 (EN_B, and_33_out, and_34_out, and_37_out, and_35_out, and_36_out);
  or or_7 (EN_A, and_27_out, and_28_out, and_29_out, Comparing, and_30_out, and_31_out, and_32_out);

  // Other names for the same wires on the sheet: LOCKED = L; UNLOCKED = U
endmodule
